# Fritzing sketch circuit (saved by Fritzing 0.9.10b)
circuit board: 5cm x 8.5cm
breadboards: 1

parts:
  Part2 = Adafruit MicroSD card breakout board [part_number="Adafruit #254"]
  F3 = Basic Flex Resistor
  Part3 = Bluetooth HC-05 Macho
  F1 = Basic Flex Resistor
  R6 = Resistor [tolerance=±5% power=0.25 resistance=2k package=THT]
  F2 = Basic Flex Resistor
  Grove1 = Grove 3 Axis Digital Accelerometer 16g
  VCC1 = Battery block 9V
  R4 = Resistor [tolerance=±5% power=0.25 resistance=10k package=THT]
  F4 = Basic Flex Resistor
  R1 = Resistor [tolerance=±5% power=0.25 resistance=10k package=THT]
  R2 = Resistor [tolerance=±5% power=0.25 resistance=10k package=THT]
  Part1 = Arduino Nano (Rev3.0)
  R5 = Resistor [tolerance=±5% power=0.25 resistance=1k package=THT]
  R3 = Resistor [tolerance=±5% power=0.25 resistance=10k package=THT]

nets:
  VCC: Part2.VCC, Part3.VCC, R4.Pin_1, R1.Pin_1, R2.Pin_1, Part1.5V, R3.Pin_1
  GND: Part2.GND, F3.pin_1, Part3.GND, F1.pin_1, R6.Pin_0, F2.pin_1, Grove1.GND, VCC1.-, F4.pin_1, Part1.GND
  N1: Part2.CLK, Part1.D13/SCK
  N2: Part2.DO, Part1.D12/MISO
  N3: Part2.DI, Part1.D11/MOSI
  N4: Part2.CS, Part1.D10
  N5: F3.Pin_2, Part1.A2, R3.Pin_0
  N6: Part3.TXD, Part1.D3
  N7: Part3.RXD, R6.Pin_1, R5.Pin_1
  N8: F1.Pin_2, R1.Pin_0, Part1.A0
  N9: F2.Pin_2, R2.Pin_0, Part1.A1
  VCC_2: Grove1.VCC, Part1.3V3
  N10: Grove1.SDA, Part1.A4
  N11: Grove1.SCL, Part1.A5
  N12: VCC1.+, Part1.VIN
  N13: R4.Pin_0, F4.Pin_2, Part1.A3
  N14: Part1.D2, R5.Pin_0

custom parts:
  Adafruit MicroSD card breakout board: Not just a simple breakout board, this microSD adapter goes the extra mile - designed for ease of use. Onboard 5v->3v regulator provides 150mA for power-hungry cards 3v level shifting means you can use this with ease on either 3v or 5v systems Uses a proper level shifting chip, not resistors: less problems, and faster read/write access Use 3 or 4 digital pins to read and write 2Gb+ of storage!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
